# Fritzing sketch joystick-neu (saved by Fritzing 1.0.0rc)
breadboards: 1

parts:
  Bauteil2 = Adafruit T-Cobbler Plus [part_number="Adafruit #1989 and #2028"]
  R1 = Resistor [tolerance=±5% power=0.25W resistance=10k package=THT]
  R2 = Resistor [tolerance=±5% power=0.25W resistance=10k package=THT]
  R3 = Resistor [tolerance=±5% power=0.25W resistance=10k package=THT]
  R4 = Resistor [tolerance=±5% power=0.25W resistance=10k package=THT]
  J1 = shrouded pin header, 10 pins [form="♂ (shrouded male)"]
  U1 = JOYSTICK-PSP1000 [package=joystick-psp1000]

nets:
  N1: Bauteil2.+3.3V, R1.Pin_1, R3.Pin_1, R4.Pin_1
  N2: Bauteil2.GND, J1.pin6
  N3: Bauteil2.EEDAT, R2.Pin_0
  N4: Bauteil2.GPIO5, R1.Pin_0, J1.pin9
  N5: Bauteil2.GPIO6, J1.pin10
  N6: Bauteil2.GPIO13, R3.Pin_0, J1.pin7
  N7: Bauteil2.GPIO19, R4.Pin_0, J1.pin8
  N8: J1.pin1, J1.pin2, U1.VCC
  N9: J1.pin3, U1.GND
  N10: J1.pin4, U1.Y
  N11: J1.pin5, U1.X

custom parts:
  Adafruit T-Cobbler Plus: The Raspberry Pi has landed on the Maker World like a 40-GPIO pinned, quad-USB ported, credit card sized bomb of DIY joy. And while you can use most of our great Model B accessories by hooking up our downgrade cable, its probably a good time to upgrade your set up and accessorize using all of the 40 pins. That's why we now carry the Assembled Adafruit Pi T-Cobbler Plus - Breakout + Cable for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
