# Fritzing sketch joystickAnalog (saved by Fritzing 0.9.3b)
breadboards: 1

parts:
  Bauteil1 = Adafruit T-Cobbler Plus [part_number="Adafruit #1989 and #2028"]
  Part1 = ADS1115  # not connected
  KY-023 = Black Joystick KY-023
  part = Resistor [tolerance=±5% resistance=10k package=THT]
  part_2 = Resistor [tolerance=±5% resistance=1k package=THT]

nets:
  +3.3V: Bauteil1.+3.3V, KY-023.+5V, part.Pin_1
  GND: Bauteil1.GND, KY-023.GND
  N1: Bauteil1.GPIO26, part.Pin_0, part_2.Pin_1
  N2: KY-023.SW, part_2.Pin_0

custom parts:
  Adafruit T-Cobbler Plus: The Raspberry Pi has landed on the Maker World like a 40-GPIO pinned, quad-USB ported, credit card sized bomb of DIY joy. And while you can use most of our great Model B accessories by hooking up our downgrade cable, its probably a good time to upgrade your set up and accessorize using all of the 40 pins. That's why we now carry the Assembled Adafruit Pi T-Cobbler Plus - Breakout + Cable for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
  ADS1115: ADC ADS1115
  Black Joystick KY-023: Description: The joystick is a combination of 2 analoog potentiometer and a digital switch. Arduino GND --> Module pin - Arduino +5V --> Module pin +5V Arduino Analoog 0 --> Module VRx Arduino Analoog 1 --> Module VRy Arduino Digital --> Module SW Dimensions: 1" x 1.25"
