# Fritzing sketch voltageDivider (saved by Fritzing 0.9.3b)
breadboards: 1

parts:
  Bauteil1 = Adafruit T-Cobbler Plus [part_number="Adafruit #1989 and #2028"]
  red = Resistor [tolerance=±5% resistance=68 package=THT]
  blue = Resistor [tolerance=±5% resistance=15 package=THT]
  green = Resistor [tolerance=±5% resistance=33 package=THT]
  LED2 = LED - 3mm [color="Red (633nm)" package="3 mm [THT]"]
  LED3 = LED - 3mm [color="Blue (505nm)" package="3 mm [THT]"]
  LED4 = LED - 3mm [color="Green (565nm)" package="3 mm [THT]"]

nets:
  N1: Bauteil1.GND, LED2.anode, LED3.anode, LED4.anode
  N2: Bauteil1.GPIO13, red.Pin_1
  N3: Bauteil1.GPIO19, blue.Pin_1
  N4: Bauteil1.GPIO26, green.Pin_1
  N5: red.Pin_0, LED2.cathode
  N6: blue.Pin_0, LED3.cathode
  N7: green.Pin_0, LED4.cathode

custom parts:
  Adafruit T-Cobbler Plus: The Raspberry Pi has landed on the Maker World like a 40-GPIO pinned, quad-USB ported, credit card sized bomb of DIY joy. And while you can use most of our great Model B accessories by hooking up our downgrade cable, its probably a good time to upgrade your set up and accessorize using all of the 40 pins. That's why we now carry the Assembled Adafruit Pi T-Cobbler Plus - Breakout + Cable for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
